// Logisim project lab1-sr_d.circ as structural Verilog: 1 circuit, main circuit main
module main (
  input  R,
  input  S,
  input  D,
  output Q,
  output Q_prime,
  output Q_2,
  output Q_prime_2
);

  wire and_1_out, and_2_out, and_3_out, and_4_out, clock_1_out, clock_2_out, not_1_out;

  Clock clock_1 (.out(clock_1_out));
  Clock clock_2 (.out(clock_2_out));
  not not_1 (not_1_out, D);
  and and_1 (and_1_out, R, clock_1_out);
  and and_2 (and_2_out, clock_1_out, S);
  and and_3 (and_3_out, not_1_out, clock_2_out);
  and and_4 (and_4_out, clock_2_out, D);
  nor nor_1 (Q_2, and_3_out, Q_prime_2);
  nor nor_2 (Q_prime_2, Q_2, and_4_out);
  nor nor_3 (Q, and_1_out, Q_prime);
  nor nor_4 (Q_prime, Q, and_2_out);

  // Notes on the sheet:
  //   CP
  //   CP
  //   S-R Flip flop
  //   D-FLIP FLOP
  //   kaushik Gupta_201900318
endmodule
