// Logisim project lab1_jk.circ as structural Verilog: 1 circuit, main circuit main
module main (
  input  T,
  output Q,
  output Q_prime
);

  wire clock_1_out, nand_1_out, nand_2_out;

  Clock clock_1 (.out(clock_1_out));
  nand nand_1 (nand_1_out, Q_prime, T, clock_1_out);
  nand nand_2 (nand_2_out, clock_1_out, T, Q);
  nand nand_3 (Q, nand_1_out, Q_prime);
  nand nand_4 (Q_prime, Q, nand_2_out);

  // Notes on the sheet:
  //   ck
  //   KaushikGupta 201900318
  //   T FLIP FLOP
endmodule
