// Logisim project exp10.circ as structural Verilog: 1 circuit, main circuit main
module main (
  input  in_1,
  output A,
  output B,
  output C,
  output D
);

  wire clock_1_out, j_k_ff_1_qn, j_k_ff_3_qn, j_k_ff_4_qn;

  Clock clock_1 (.out(clock_1_out));
  J_K_Flip_Flop j_k_ff_1 (
    .J(D), .clk(clock_1_out), .K(j_k_ff_4_qn), .Q(A), .Qn(j_k_ff_1_qn), .preset(in_1));  // open: en, reset
  J_K_Flip_Flop j_k_ff_2 (
    .J(A), .clk(clock_1_out), .K(j_k_ff_1_qn), .Q(B), .Qn(clock_1_out), .reset(in_1));  // open: preset, en
  J_K_Flip_Flop j_k_ff_3 (
    .J(B), .clk(clock_1_out), .K(clock_1_out), .Q(C), .Qn(j_k_ff_3_qn), .reset(in_1));  // open: preset, en
  J_K_Flip_Flop j_k_ff_4 (
    .J(C), .clk(clock_1_out), .K(j_k_ff_3_qn), .Q(D), .Qn(j_k_ff_4_qn), .reset(in_1));  // open: preset, en

  // Notes on the sheet:
  //   CK
  //   lsb
  //   KAUSHIK GUPTA-201900318
  //   4bit ring counter
  //   msb
endmodule
