// Logisim project exp11.circ as structural Verilog: 1 circuit, main circuit main
module main (
  output b,
  output a,
  output c,
  output d
);

  wire clock_1_out, j_k_ff_1_qn, j_k_ff_2_qn, j_k_ff_3_qn, j_k_ff_4_qn;

  Clock clock_1 (.out(clock_1_out));
  J_K_Flip_Flop j_k_ff_1 (
    .J(j_k_ff_4_qn), .clk(clock_1_out), .K(d), .Q(a), .Qn(j_k_ff_1_qn));  // open: preset, en, reset
  J_K_Flip_Flop j_k_ff_2 (
    .J(a), .clk(clock_1_out), .K(j_k_ff_1_qn), .Q(b), .Qn(j_k_ff_2_qn));  // open: preset, en, reset
  J_K_Flip_Flop j_k_ff_3 (
    .J(b), .clk(clock_1_out), .K(j_k_ff_2_qn), .Q(c), .Qn(j_k_ff_3_qn));  // open: preset, en, reset
  J_K_Flip_Flop j_k_ff_4 (
    .J(c), .clk(clock_1_out), .K(j_k_ff_3_qn), .Q(d), .Qn(j_k_ff_4_qn));  // open: preset, en, reset

  // Notes on the sheet:
  //   ck
  //   lsb
  //   kaushik gupta-201900318
  //   johson counter 4bit
  //   msb
endmodule
