// Logisim project exp12.circ as structural Verilog: 1 circuit, main circuit main
module main (
  input  in_1,
  output out_2,
  output out_3,
  output out_4
);

  wire and_1_out, and_2_out, and_3_out, clock_1_out, d_ff_1_qn, d_ff_2_qn, d_ff_3_qn, or_1_out;

  Clock clock_1 (.out(clock_1_out));
  or or_1 (or_1_out, and_1_out, and_2_out);
  D_Flip_Flop d_ff_1 (.clk(clock_1_out), .D(or_1_out), .Q(out_2), .Qn(d_ff_1_qn));  // open: preset, en, reset
  and and_1 (and_1_out, d_ff_1_qn, out_3, d_ff_3_qn);
  and and_2 (and_2_out, out_2, d_ff_2_qn, d_ff_3_qn);
  D_Flip_Flop d_ff_2 (.clk(clock_1_out), .D(and_3_out), .Q(out_3), .Qn(d_ff_2_qn));  // open: preset, en, reset
  and and_3 (and_3_out, d_ff_2_qn, d_ff_3_qn);
  D_Flip_Flop d_ff_3 (.clk(clock_1_out), .D(in_1), .Q(out_4), .Qn(d_ff_3_qn));  // open: preset, en, reset

  // Notes on the sheet:
  //   A
  //   kaushik gupta 201900318
  //   B
  //   C
endmodule
