// Logisim project JK2D&JK2T.circ as structural Verilog: 1 circuit, main circuit main
module main (
  input  j,
  input  D,
  input  k,
  input  T,
  input  T_2,
  output Q,
  output Q_2,
  output Q_prime,
  output Q_prime_2,
  output Q_3,
  output Q_prime_3,
  output Q_4,
  output Q_prime_4
);

  wire and_1_out, and_2_out, clock_1_out, clock_2_out, clock_3_out, clock_4_out, not_1_out, not_2_out,
       or_1_out, xor_1_out;

  Clock clock_1 (.out(clock_1_out));
  not not_1 (not_1_out, D);
  Clock clock_2 (.out(clock_2_out));
  J_K_Flip_Flop j_k_ff_1 (.J(D), .clk(clock_1_out), .K(not_1_out), .Q(Q), .Qn(Q_prime));  // open: preset, en, reset
  J_K_Flip_Flop #(.trigger("falling")) j_k_ff_2 (
    .J(T), .clk(clock_2_out), .K(T), .Q(Q_4), .Qn(Q_prime_4));  // open: preset, en, reset
  not not_2 (not_2_out, k);
  Clock clock_3 (.out(clock_3_out));
  and and_1 (and_1_out, j, Q_prime_2);
  and and_2 (and_2_out, not_2_out, Q_2);
  or or_1 (or_1_out, and_1_out, and_2_out);
  D_Flip_Flop d_ff_1 (.clk(clock_3_out), .D(or_1_out), .Q(Q_2), .Qn(Q_prime_2));  // open: preset, en, reset
  Clock clock_4 (.out(clock_4_out));
  xor xor_1 (xor_1_out, Q_3, T_2);
  D_Flip_Flop d_ff_2 (.clk(clock_4_out), .D(xor_1_out), .Q(Q_3), .Qn(Q_prime_3));  // open: preset, en, reset

  // Notes on the sheet:
  //   CK
  //   Ck
  //   kaushikGupta 201900318
  //   jk to d flip flop
  //   kaushikGupta 201900318
  //   jk to T flip flop
  //   D to JK FF
  //   kaushikGupta 201900318
  //   KAUSHIKGUPTA_201900318
  //   D TO T FF
endmodule
