// Logisim project mod10.circ as structural Verilog: 1 circuit, main circuit main
module main (
  input  I,
  output QA,
  output QB,
  output QC,
  output QD
);

  wire and_1_out, CLK_out, not_1_out, not_2_out;

  Clock CLK (.out(CLK_out));
  J_K_Flip_Flop #(.trigger("falling")) j_k_ff_1 (
    .J(I), .clk(CLK_out), .K(I), .Q(QA), .reset(and_1_out));  // open: Qn, preset, en
  not not_1 (not_1_out, QA);
  J_K_Flip_Flop #(.trigger("falling")) j_k_ff_2 (
    .J(I), .clk(QA), .K(I), .Q(QB), .reset(and_1_out));  // open: Qn, preset, en
  J_K_Flip_Flop #(.trigger("falling")) j_k_ff_3 (
    .J(I), .clk(QB), .K(I), .Q(QC), .reset(and_1_out));  // open: Qn, preset, en
  and and_1 (and_1_out, not_1_out, QB, not_2_out, QD);
  not not_2 (not_2_out, QC);
  J_K_Flip_Flop #(.trigger("falling")) j_k_ff_4 (
    .J(I), .clk(QC), .K(I), .Q(QD), .reset(and_1_out));  // open: Qn, preset, en

  // Notes on the sheet:
  //   Kauhik gupta 
  //   201900318
  //   MOD 10 ASYNCHRONOUS COUNTER/ decade 
endmodule
