// Logisim project mod16_10counter.circ as structural Verilog: 1 circuit, main circuit main
module main (
  input  in_1,
  output Qd,
  output Qc,
  output Qb,
  output MSB
);

  wire clock_1_out;

  Clock clock_1 (.out(clock_1_out));
  J_K_Flip_Flop #(.trigger("falling")) j_k_ff_1 (
    .J(in_1), .clk(clock_1_out), .K(in_1), .Q(Qd));  // open: Qn, preset, en, reset
  J_K_Flip_Flop #(.trigger("falling")) j_k_ff_2 (.J(in_1), .clk(Qd), .K(in_1), .Q(Qc));  // open: Qn, preset, en, reset
  J_K_Flip_Flop #(.trigger("falling")) j_k_ff_3 (.J(in_1), .clk(Qc), .K(in_1), .Q(Qb));  // open: Qn, preset, en, reset
  J_K_Flip_Flop #(.trigger("falling")) j_k_ff_4 (.J(in_1), .clk(Qb), .K(in_1), .Q(MSB));  // open: Qn, preset, en, reset

  // Notes on the sheet:
  //   CK
  //   LSB
  //   Mod 16 Counter
  //   kaushikGupta_201900318
  //   Qa
endmodule
