// Logisim project mod8Up_downcounter.circ as structural Verilog: 1 circuit, main circuit main
module main (
  input  DOWN,
  input  E,
  input  UP,
  output LSB,
  output Qb,
  output Qa
);

  wire clock_1_out, j_k_ff_1_qn, j_k_ff_2_qn, nand_1_out, nand_2_out, nand_3_out, nand_4_out, nand_5_out,
       nand_6_out;

  Clock clock_1 (.out(clock_1_out));
  nand nand_1 (nand_1_out, j_k_ff_1_qn, UP);
  nand nand_2 (nand_2_out, DOWN, LSB);
  J_K_Flip_Flop j_k_ff_1 (.J(E), .clk(clock_1_out), .K(E), .Q(LSB), .Qn(j_k_ff_1_qn));  // open: preset, en, reset
  J_K_Flip_Flop j_k_ff_2 (.J(E), .clk(nand_3_out), .K(E), .Q(Qb), .Qn(j_k_ff_2_qn));  // open: preset, en, reset
  nand nand_3 (nand_3_out, nand_2_out, nand_1_out);
  nand nand_4 (nand_4_out, DOWN, Qb);
  nand nand_5 (nand_5_out, j_k_ff_2_qn, UP);
  nand nand_6 (nand_6_out, nand_4_out, nand_5_out);
  J_K_Flip_Flop j_k_ff_3 (.J(E), .clk(nand_6_out), .K(E), .Q(Qa));  // open: Qn, preset, en, reset

  // Notes on the sheet:
  //   CK
  //   Qc
  //   Kaushik gupta
  //   201900318
  //   MSB
endmodule
