// Logisim project sync16_upcounter.circ as structural Verilog: 1 circuit, main circuit main
module main (
  input  _1,
  output out_2,
  output B,
  output C,
  output D
);

  wire and_1_out, and_2_out, clock_1_out;

  Clock clock_1 (.out(clock_1_out));
  and and_1 (and_1_out, B, and_2_out);
  J_K_Flip_Flop j_k_ff_1 (.J(and_1_out), .clk(clock_1_out), .K(and_1_out), .Q(out_2));  // open: Qn, preset, en, reset
  and and_2 (and_2_out, C, D);
  J_K_Flip_Flop j_k_ff_2 (.J(and_2_out), .clk(clock_1_out), .K(and_2_out), .Q(B));  // open: Qn, preset, en, reset
  J_K_Flip_Flop j_k_ff_3 (.J(D), .clk(clock_1_out), .K(D), .Q(C));  // open: Qn, preset, en, reset
  J_K_Flip_Flop j_k_ff_4 (.J(_1), .clk(clock_1_out), .K(_1), .Q(D));  // open: Qn, preset, en, reset

  // Notes on the sheet:
  //   cp
  //   MSB
  //   A
  //   201900318 KAUSHIK GUPTA
  //   LSB
endmodule
