// Logisim project doubtful_counter.circ as structural Verilog: 1 circuit, main circuit main
module main (
  input  CTR,
  output A,
  output B
);

  wire clock_1_out, d_ff_2_qn, xor_1_out;

  Clock clock_1 (.out(clock_1_out));
  ExactlyOne xor_1 (.out(xor_1_out), .in0(CTR), .in1(A), .in2(B));
  D_Flip_Flop d_ff_1 (.clk(clock_1_out), .D(xor_1_out), .Q(A));  // open: Qn, preset, en, reset
  D_Flip_Flop d_ff_2 (.clk(clock_1_out), .D(d_ff_2_qn), .Q(B), .Qn(d_ff_2_qn));  // open: preset, en, reset

  // Notes on the sheet:
  //   0-UP
  //   1-DOWN
  //   CK
  //   KAUSHIK GUPTA 201900318
  //   MSB
  //   LSB
endmodule
