// Logisim project ringCounter_4bit.circ as structural Verilog: 1 circuit, main circuit main
module main (
  input  CLR,
  input  P_SET,
  input  P_SET_2,
  output Qa,
  output Qb,
  output Qc,
  output Qd
);

  wire clock_1_out;

  Clock clock_1 (.out(clock_1_out));
  D_Flip_Flop d_ff_1 (.clk(Qd), .D(clock_1_out), .Q(Qa), .preset(P_SET), .reset(CLR));  // open: Qn, en
  D_Flip_Flop d_ff_2 (.clk(Qa), .D(clock_1_out), .Q(Qb), .preset(P_SET_2), .reset(CLR));  // open: Qn, en
  D_Flip_Flop d_ff_3 (.clk(Qb), .D(clock_1_out), .Q(Qc), .preset(P_SET_2), .reset(CLR));  // open: Qn, en
  D_Flip_Flop d_ff_4 (.clk(Qc), .D(clock_1_out), .Q(Qd), .preset(P_SET_2), .reset(CLR));  // open: Qn, en

  // Notes on the sheet:
  //   CK
  //   Kaushik gupta_201900318
endmodule
