// Logisim project JOHNSON COUNTER.circ as structural Verilog: 1 circuit, main circuit main
module main (
  output QA,
  output QB,
  output QC,
  output QD
);

  wire CLK_out, DD_qn;

  Clock CLK (.out(CLK_out));
  D_Flip_Flop DA (.clk(CLK_out), .D(DD_qn), .Q(QA));  // open: Qn, preset, en, reset
  D_Flip_Flop DB (.clk(CLK_out), .D(QA), .Q(QB));  // open: Qn, preset, en, reset
  D_Flip_Flop DC (.clk(CLK_out), .D(QB), .Q(QC));  // open: Qn, preset, en, reset
  D_Flip_Flop DD (.clk(CLK_out), .D(QC), .Q(QD), .Qn(DD_qn));  // open: preset, en, reset

  // Notes on the sheet:
  //   MSB
  //   Kaushik Gupta
  //   201900318
  //   4 BIT TWISTED RING OR JOHNSON COUNTER
  //   LSB
endmodule
