// Logisim project AND GATE.circ as structural Verilog: 1 circuit, main circuit main
module main (
  input  A,
  input  A_2,
  input  B,
  input  B_2,
  input  A_3,
  input  A_4,
  input  B_3,
  input  B_4,
  output C,
  output C_2,
  output C_3,
  output C_4
);

  and and_1 (C, A, B);
  and and_2 (C_4, A_4, B_4);
  and and_3 (C_2, A_2, B_2);
  and and_4 (C_3, A_3, B_3);

  // Notes on the sheet:
  //   AND GATE  (C=A.B)
endmodule
