// Logisim project BINARY TO GRAY.circ as structural Verilog: 1 circuit, main circuit main
module main (
  input  W,
  input  X,
  input  Y,
  input  Z,
  output A,
  output B,
  output C,
  output D
);

  xor xor_1 (B, W, X);
  xor xor_2 (C, X, Y);
  xor xor_3 (D, Y, Z);

  assign A = W;

  // Notes on the sheet:
  //   REGISTRATION NUMBER: 201900179
  //   NAME:KAMBHAMPATI MAHESH MANIKANTA
endmodule
