// Logisim project COUNTER.circ as structural Verilog: 1 circuit, main circuit main
module main (
  input  I,
  output QA,
  output QB,
  output QC,
  output QD
);

  wire CLK_out, nand_1_out;

  Clock CLK (.out(CLK_out));
  J_K_Flip_Flop #(.trigger("falling")) j_k_ff_1 (
    .J(I), .clk(CLK_out), .K(I), .Q(QA), .en(nand_1_out));  // open: Qn, preset, reset
  J_K_Flip_Flop #(.trigger("falling")) j_k_ff_2 (
    .J(I), .clk(QA), .K(I), .Q(QB), .en(nand_1_out));  // open: Qn, preset, reset
  J_K_Flip_Flop #(.trigger("falling")) j_k_ff_3 (
    .J(I), .clk(QB), .K(I), .Q(QC), .en(nand_1_out));  // open: Qn, preset, reset
  nand nand_1 (nand_1_out, QB, QD);
  J_K_Flip_Flop #(.trigger("falling")) j_k_ff_4 (
    .J(I), .clk(QC), .K(I), .Q(QD), .en(nand_1_out));  // open: Qn, preset, reset

  // Notes on the sheet:
  //   Kauhik gupta 
  //   201900318
  //   MOD 10 ASYNCHRONOUS COUNTER
endmodule
