// Logisim project D FLIPFLOP.circ as structural Verilog: 1 circuit, main circuit main
module main (
  input  CP,
  input  D,
  output Q,
  output Q_prime
);

  wire and_1_out, and_2_out, not_1_out;

  not not_1 (not_1_out, D);
  and and_1 (and_1_out, not_1_out, CP);
  and and_2 (and_2_out, CP, D);
  nor nor_1 (Q, and_1_out, Q_prime);
  nor nor_2 (Q_prime, Q, and_2_out);

  // Notes on the sheet:
  //   201900179
  //   D FLIPFLOP
  //   KAMBHAMPATI MAHESH MANIKANTA
endmodule
