// Logisim project DECODER.circ as structural Verilog: 1 circuit, main circuit main
module main (
  input  A,
  input  B,
  output D0,
  output D1,
  output D2,
  output D3
);

  wire not_1_out, not_2_out;

  not not_1 (not_1_out, A);
  not not_2 (not_2_out, B);
  and and_1 (D0, not_1_out, not_2_out);
  and and_2 (D1, not_1_out, B);
  and and_3 (D2, A, not_2_out);
  and and_4 (D3, A, B);

  // Notes on the sheet:
  //   KAMBHAMPATI MAHESH MANIKANTA
  //   201900179
  //   2 TO 4 DECODER
endmodule
