// Logisim project HALF ADDER.circ as structural Verilog: 1 circuit, main circuit main
module main (
  input  A,
  input  B,
  output C,
  output S
);

  and and_1 (C, A, B);
  xor xor_1 (S, A, B);

  // Notes on the sheet:
  //   REGISTRATION NUMBER : 201900179
  //   HALF ADDER CIRCUIT
  //   NAME: KAMBHAMPATI MAHESH MANIKANTA
endmodule
