// Logisim project HALF SUBRACTOR.circ as structural Verilog: 1 circuit, main circuit main
module main (
  input  A,
  input  B,
  output BOR,
  output D
);

  wire not_1_out;

  not not_1 (not_1_out, A);
  and and_1 (BOR, not_1_out, B);
  xor xor_1 (D, A, B);

  // Notes on the sheet:
  //   NAME: KAMBHAMPATI MAHESH MANIKANTA
  //   REGISTRATION NUMBER:201900179
  //   HALF SUBRACTOR CIRCUIT
endmodule
