// Logisim project HALFADDER USING NAND GATE.circ as structural Verilog: 1 circuit, main circuit main
module main (
  input  A,
  input  B,
  output CARRY,
  output SUM
);

  wire nand_1_out, nand_2_out, nand_3_out, nand_4_out;

  nand nand_1 (nand_1_out, A, B);
  nand nand_2 (nand_2_out, A, B);
  nand nand_3 (nand_3_out, A, nand_1_out);
  nand nand_4 (nand_4_out, nand_1_out, B);
  nand nand_5 (CARRY, nand_2_out, nand_2_out);
  nand nand_6 (SUM, nand_3_out, nand_4_out);

  // Notes on the sheet:
  //   KAMBHAMPATI MAHESH MANIKANTA
  //   201900179
  //   HALF ADDER USING NAND GATE
endmodule
