// Logisim project MOD 16 DOWN COUNTER.circ as structural Verilog: 1 circuit, main circuit main
module main (
  output QA,
  output QB,
  output QC,
  output QD
);

  wire CLK_out, d_ff_1_qn, d_ff_2_qn, d_ff_3_qn, d_ff_4_qn;

  Clock CLK (.out(CLK_out));
  D_Flip_Flop d_ff_1 (.clk(CLK_out), .D(d_ff_1_qn), .Q(QA), .Qn(d_ff_1_qn));  // open: preset, en, reset
  D_Flip_Flop d_ff_2 (.clk(QA), .D(d_ff_2_qn), .Q(QB), .Qn(d_ff_2_qn));  // open: preset, en, reset
  D_Flip_Flop d_ff_3 (.clk(QB), .D(d_ff_3_qn), .Q(QC), .Qn(d_ff_3_qn));  // open: preset, en, reset
  D_Flip_Flop d_ff_4 (.clk(QC), .D(d_ff_4_qn), .Q(QD), .Qn(d_ff_4_qn));  // open: preset, en, reset

  // Notes on the sheet:
  //   D FLIPFLOP 1
  //   D FLIPFLOP 2
  //   KAMBHAMPATI MAHESH MANIKANTA
  //   201900179
  //   MOD 16 ASYNCHRONUS DOWN COUNTER
  //   D FLIPFLOP 3
  //   D FLIPFLOP 4
endmodule
