// Logisim project NAND GATE.circ as structural Verilog: 1 circuit, main circuit main
module main (
  input  U,
  input  U_2,
  input  V,
  input  V_2,
  input  U_3,
  input  U_4,
  input  V_3,
  input  V_4,
  output W,
  output W_2,
  output W_3,
  output W_4
);

  nand nand_1 (W, U, V);
  nand nand_2 (W_4, U_4, V_4);
  nand nand_3 (W_2, U_2, V_2);
  nand nand_4 (W_3, U_3, V_3);

  // Notes on the sheet:
  //   NAND GATE
endmodule
