// Logisim project NOR GATE.circ as structural Verilog: 1 circuit, main circuit main
module main (
  input  I,
  input  I_2,
  input  J,
  input  J_2,
  input  I_3,
  input  I_4,
  input  J_3,
  input  J_4,
  output K,
  output K_2,
  output K_3,
  output K_4
);

  nor nor_1 (K, I, J);
  nor nor_2 (K_4, I_4, J_4);
  nor nor_3 (K_2, I_2, J_2);
  nor nor_4 (K_3, I_3, J_3);

  // Notes on the sheet:
  //   NOR GATE
endmodule
