// Logisim project NOT GATE.circ as structural Verilog: 1 circuit, main circuit main
module main (
  input  M,
  input  M_2,
  output N,
  output N_2
);

  not not_1 (N_2, M_2);
  not not_2 (N, M);

  // Notes on the sheet:
  //   NOT GATE 
endmodule
