// Logisim project ONE BIT COMPARATOR.circ as structural Verilog: 1 circuit, main circuit main
module main (
  input  A,
  input  B,
  output X,
  output Y,
  output Z
);

  wire not_1_out, not_2_out, xor_1_out;

  not not_1 (not_1_out, A);
  not not_2 (not_2_out, B);
  and and_1 (X, not_1_out, B);
  xor xor_1 (xor_1_out, A, B);
  and and_2 (Z, A, not_2_out);
  not not_3 (Y, xor_1_out);

  // Notes on the sheet:
  //   A<B
  //   A=B
  //   A>B
endmodule
