// Logisim project OR GATE.circ as structural Verilog: 1 circuit, main circuit main
module main (
  input  X,
  input  X_2,
  input  Y,
  input  Y_2,
  input  X_3,
  input  X_4,
  input  Y_3,
  input  Y_4,
  output Z,
  output Z_2,
  output Z_3,
  output Z_4
);

  or or_1 (Z, X, Y);
  or or_2 (Z_4, X_4, Y_4);
  or or_3 (Z_2, X_2, Y_2);
  or or_4 (Z_3, X_3, Y_3);

  // Notes on the sheet:
  //   OR GATE 
endmodule
