// Logisim project PIPO.circ as structural Verilog: 1 circuit, main circuit main
module main (
  input  QA,
  input  QB,
  input  QC,
  input  QD,
  output QA_2,
  output QB_2,
  output QC_2,
  output QD_2
);

  wire CLK_out;

  Clock CLK (.out(CLK_out));
  D_Flip_Flop DA (.clk(CLK_out), .D(QA), .Q(QA_2));  // open: Qn, preset, en, reset
  D_Flip_Flop DB (.clk(CLK_out), .D(QB), .Q(QB_2));  // open: Qn, preset, en, reset
  D_Flip_Flop DC (.clk(CLK_out), .D(QC), .Q(QC_2));  // open: Qn, preset, en, reset
  D_Flip_Flop DD (.clk(CLK_out), .D(QD), .Q(QD_2));  // open: Qn, preset, en, reset

  // Notes on the sheet:
  //   KAMBHAMPATI MAHESH MANIKANTA
  //   201900179
  //   PARALLEL  IN PARALLEL OUT (PIPO)
  //   <---------------------------------------------DATA INPUT ------------------------------->
  //   <---------------------------------------------DATA OUTPUT----------------------------------->
endmodule
