// Logisim project PISO.circ as structural Verilog: 1 circuit, main circuit main
module main (
  input  QA,
  input  QB,
  input  QC,
  input  QD,
  input  C,
  output DATA_OUTPUT
);

  wire CLK_out, DA_q, DB_q, DC_q, multiplexer_1_out, multiplexer_2_out, multiplexer_3_out;

  Clock CLK (.out(CLK_out));
  D_Flip_Flop DA (.clk(CLK_out), .D(QA), .Q(DA_q));  // open: Qn, preset, en, reset
  Multiplexer #(.enable("false")) multiplexer_1 (.in0(QB), .in1(DA_q), .out(multiplexer_1_out), .sel(C));
  D_Flip_Flop DB (.clk(CLK_out), .D(multiplexer_1_out), .Q(DB_q));  // open: Qn, preset, en, reset
  Multiplexer #(.enable("false")) multiplexer_2 (.in0(QC), .in1(DB_q), .out(multiplexer_2_out), .sel(C));
  D_Flip_Flop DC (.clk(CLK_out), .D(multiplexer_2_out), .Q(DC_q));  // open: Qn, preset, en, reset
  Multiplexer #(.enable("false")) multiplexer_3 (.in0(QD), .in1(DC_q), .out(multiplexer_3_out), .sel(C));
  D_Flip_Flop DD (.clk(CLK_out), .D(multiplexer_3_out), .Q(DATA_OUTPUT));  // open: Qn, preset, en, reset

  // Notes on the sheet:
  //   KAMBHAMPATI MAHESH MANIKANTA
  //   201900179
  //   PARALLEL  IN SERIAL OUT (PISO)
  //   <---------------------------------------------DATA INPUT --------------------------------------->
endmodule
