// Logisim project SIPO.circ as structural Verilog: 1 circuit, main circuit main
module main (
  input  DATA_IN,
  output QA,
  output QB,
  output QC,
  output QD
);

  wire CLK_out;

  Clock CLK (.out(CLK_out));
  D_Flip_Flop DA (.clk(CLK_out), .D(DATA_IN), .Q(QA));  // open: Qn, preset, en, reset
  D_Flip_Flop DB (.clk(CLK_out), .D(QA), .Q(QB));  // open: Qn, preset, en, reset
  D_Flip_Flop DC (.clk(CLK_out), .D(QB), .Q(QC));  // open: Qn, preset, en, reset
  D_Flip_Flop DD (.clk(CLK_out), .D(QC), .Q(QD));  // open: Qn, preset, en, reset

  // Notes on the sheet:
  //   KAMBHAMPATI MAHESH MANIKANTA
  //   201900179
  //   SERIAL  IN PARALLEL OUT (SIPO)
  //   <----------------------DATA OUTPUT------------------------------->
endmodule
