// Logisim project SISO.circ as structural Verilog: 1 circuit, main circuit main
module main (
  input  DATA_IN,
  output DATA_OUT
);

  wire CLK_out, DA_q, DB_q, DC_q;

  Clock CLK (.out(CLK_out));
  D_Flip_Flop DA (.clk(CLK_out), .D(DATA_IN), .Q(DA_q));  // open: Qn, preset, en, reset
  D_Flip_Flop DB (.clk(CLK_out), .D(DA_q), .Q(DB_q));  // open: Qn, preset, en, reset
  D_Flip_Flop DC (.clk(CLK_out), .D(DB_q), .Q(DC_q));  // open: Qn, preset, en, reset
  D_Flip_Flop DD (.clk(CLK_out), .D(DC_q), .Q(DATA_OUT));  // open: Qn, preset, en, reset

  // Notes on the sheet:
  //   KAMBHAMPATI MAHESH MANIKANTA
  //   201900179
  //   SERIAL IN SERIAL OUT (SISO)
endmodule
