// Logisim project XNOR GATE.circ as structural Verilog: 1 circuit, main circuit main
module main (
  input  Q,
  input  Q_2,
  input  R,
  input  R_2,
  input  Q_3,
  input  Q_4,
  input  R_3,
  input  R_4,
  output S,
  output S_2,
  output S_3,
  output S_4
);

  xnor xnor_1 (S, Q, R);
  xnor xnor_2 (S_4, Q_4, R_4);
  xnor xnor_3 (S_2, Q_2, R_2);
  xnor xnor_4 (S_3, Q_3, R_3);

  // Notes on the sheet:
  //   XNOR GATE 
endmodule
