// Logisim project XOR GATE.circ as structural Verilog: 1 circuit, main circuit main
module main (
  input  E,
  input  E_2,
  input  F,
  input  F_2,
  input  E_3,
  input  E_4,
  input  F_3,
  input  F_4,
  output G,
  output G_2,
  output G_3,
  output G_4
);

  xor xor_1 (G, E, F);
  xor xor_2 (G_4, E_4, F_4);
  xor xor_3 (G_2, E_2, F_2);
  xor xor_4 (G_3, E_3, F_3);

  // Notes on the sheet:
  //   XOR GATE
endmodule
