// Logisim project multiprexer.circ as structural Verilog: 1 circuit, main circuit main
module main (
  input  A,
  input  B,
  input  I0,
  input  I1,
  input  I2,
  input  I3,
  output Y
);

  wire and_1_out, and_2_out, and_3_out, and_4_out, not_1_out, not_2_out;

  not not_1 (not_1_out, A);
  not not_2 (not_2_out, B);
  and and_1 (and_1_out, not_1_out, I0, not_2_out);
  and and_2 (and_2_out, not_1_out, I1, B);
  and and_3 (and_3_out, A, I2, not_2_out);
  and and_4 (and_4_out, B, I3, A);
  or or_1 (Y, and_1_out, and_2_out, and_3_out, and_4_out);

  // Notes on the sheet:
  //   201900179
  //   KAMBHAMPATI MAHESH MANIKANTA 
endmodule
