// Logisim project up_counter.circ as structural Verilog: 1 circuit, main circuit main
module main (
  input  IN,
  output QC,
  output QD,
  output QA,
  output QB
);

  wire and_1_out, and_2_out, CLK_out;

  Clock CLK (.out(CLK_out));
  J_K_Flip_Flop j_k_ff_1 (.J(IN), .clk(CLK_out), .K(IN), .Q(QA));  // open: Qn, preset, en, reset
  J_K_Flip_Flop j_k_ff_2 (.J(QA), .clk(CLK_out), .K(QA), .Q(QB));  // open: Qn, preset, en, reset
  and and_1 (and_1_out, QA, QB);
  J_K_Flip_Flop j_k_ff_3 (.J(and_1_out), .clk(CLK_out), .K(and_1_out), .Q(QC));  // open: Qn, preset, en, reset
  and and_2 (and_2_out, and_1_out, QC);
  J_K_Flip_Flop j_k_ff_4 (.J(and_2_out), .clk(CLK_out), .K(and_2_out), .Q(QD));  // open: Qn, preset, en, reset

  // Notes on the sheet:
  //   KAMBHAMPATI MAHESH MANIKANTA
  //   201900179
  //   SYNCHRONUS UP COUNTER
endmodule
